// Digital circuit CPU.dig as structural Verilog
module CPU (
  input  [63:0] Databus_Manual_Input,
  input  CPU_Clock,
  input  in_3,
  input  in_4,
  input  in_5,
  input  in_6
);

  wire clock, Databus_Manual_Switch_out, Manual_Clock_Stepper_out, Manual_Stepping_out;
  wire [63:0] databus, Register_A_q, Register_B_q;

  Register #(.Bits(64)) Register_A (.D(databus), .C(clock), .en(in_4), .Q(Register_A_q));
  Register #(.Bits(64)) Register_B (.D(databus), .C(clock), .en(in_6), .Q(Register_B_q));
  DipSwitch #(.dipDefault("true")) Manual_Stepping (.out(Manual_Stepping_out));
  Button Manual_Clock_Stepper (.out(Manual_Clock_Stepper_out));
  assign clock = Manual_Stepping_out ? Manual_Clock_Stepper_out : 1'bz;  // Driver driver_1
  assign clock = ~Manual_Stepping_out ? CPU_Clock : 1'bz;  // DriverInvSel driverinvsel_1
  assign databus = Databus_Manual_Switch_out ? Databus_Manual_Input : 64'bz;  // Driver driver_2
  DipSwitch Databus_Manual_Switch (.out(Databus_Manual_Switch_out));
  assign databus = in_3 ? Register_A_q : 64'bz;  // Driver driver_3
  assign databus = in_5 ? Register_B_q : 64'bz;  // Driver driver_4

  // Other names for the same wires on the sheet: RAr = in_3; RAw = in_4; RBr = in_5; RBw = in_6

  // Notes on the sheet:
  //   Clock Control
  //   Manual Databus Control
  //   Register A
  //   Register B
endmodule
